# Fritzing sketch FRITZINGSCHEMATICOriginal (saved by Fritzing 0.9.3b)
breadboards: 1

parts:
  U1 = ESP8266 NodeMCU LoLin module
  J1 = Basic Servo
  U2 = BATTERY-2 [package=battery-aa]
  U3 = BATTERY-2 [package=battery-aa]
  S1 = SPST Switch [package=switch-spdt-smd]
  J2 = Basic Servo

nets:
  N1: U1.D1, J1.pulse
  N2: U1.D2, J2.pulse
  GND: U1.GND, U3.-1, J2.gnd
  VCC: U1.Vin, J1.vcc, S1.P, J2.vcc
  N3: U2.-1, U3.+1
  N4: U2.+1, S1.O

custom parts:
  ESP8266 NodeMCU LoLin module: ESP8266 based NodeMCU
